# Fritzing sketch 02_rgb_led (saved by Fritzing 0.9.5d)
breadboards: 1

parts:
  R1 = Resistor [tolerance=±5% resistance=220 package=THT]
  R2 = Resistor [tolerance=±5% resistance=220 package=THT]
  R3 = Resistor [tolerance=±5% resistance=220 package=THT]
  LED1 = RGB LED (com. cathode, rgb) [package="5 mm [THT]"]
  Parça1 = Arduino Uno (Rev3)

nets:
  N1: R1.Pin_0, Parça1.D10_PWM/SS
  N2: R1.Pin_1, LED1.green_anode
  N3: R2.Pin_0, Parça1.D11_PWM/MOSI
  N4: R2.Pin_1, LED1.blue_anode
  N5: R3.Pin_0, Parça1.D9_PWM
  N6: R3.Pin_1, LED1.red_anode
  N7: LED1.common_cathode, Parça1.GND
