# Fritzing sketch 03_button_led (saved by Fritzing 0.9.5d)
breadboards: 1

parts:
  Parça1 = Arduino Uno (Rev3)
  S1 = Pushbutton [package="[THT]"]
  R1 = Resistor [tolerance=±5% resistance=10k package=THT]
  R2 = Resistor [tolerance=±5% resistance=10k package=THT]
  LED1 = LED - 5mm [color="Red (633nm)" package="5 mm [THT]"]

nets:
  N1: Parça1.D8, S1.Pin_1, S1.Pin_2, R1.Pin_0
  N2: Parça1.D10_PWM/SS, R2.Pin_0
  N3: Parça1.5V, S1.Pin_3, S1.Pin_4
  N4: Parça1.GND, R1.Pin_1, LED1.cathode
  N5: R2.Pin_1, LED1.anode
