# Fritzing sketch 04_karasimsek (saved by Fritzing 0.9.5d)
breadboards: 1

parts:
  Parça1 = Arduino Uno (Rev3)
  R1 = Resistor [tolerance=±5% resistance=220 package=THT]
  R2 = Resistor [tolerance=±5% resistance=220 package=THT]
  R3 = Resistor [tolerance=±5% resistance=220 package=THT]
  R4 = Resistor [tolerance=±5% resistance=220 package=THT]
  R5 = Resistor [tolerance=±5% resistance=220 package=THT]
  R6 = Resistor [tolerance=±5% resistance=220 package=THT]
  LED1 = LED - 5mm [color="Red (633nm)" package="5 mm [THT]"]
  LED2 = LED - 5mm [color="Red (633nm)" package="5 mm [THT]"]
  LED3 = LED - 5mm [color="Red (633nm)" package="5 mm [THT]"]
  LED4 = LED - 5mm [color="Red (633nm)" package="5 mm [THT]"]
  LED5 = LED - 5mm [color="Red (633nm)" package="5 mm [THT]"]
  LED6 = LED - 5mm [color="Red (633nm)" package="5 mm [THT]"]

nets:
  N1: Parça1.GND, LED1.cathode, LED2.cathode, LED3.cathode, LED4.cathode, LED5.cathode, LED6.cathode
  N2: Parça1.D2, R6.Pin_0
  N3: Parça1.D3_PWM, R1.Pin_0
  N4: Parça1.D4, R5.Pin_0
  N5: Parça1.D5_PWM, R3.Pin_0
  N6: Parça1.D6_PWM, R2.Pin_0
  N7: Parça1.D7, R4.Pin_0
  N8: R1.Pin_1, LED6.anode
  N9: R2.Pin_1, LED5.anode
  N10: R3.Pin_1, LED2.anode
  N11: R4.Pin_1, LED3.anode
  N12: R5.Pin_1, LED4.anode
  N13: R6.Pin_1, LED1.anode
