# Fritzing sketch 06_hcsr04_mesafe (saved by Fritzing 0.9.5d)
breadboards: 1

parts:
  Parça1 = Arduino Uno (Rev3)
  Parça2 = HC-SR 04

nets:
  N1: Parça1.D8, Parça2.Trig
  N2: Parça1.D7, Parça2.Echo
  5V: Parça1.5V, Parça2.VCC
  GND: Parça1.GND, Parça2.GND
