# Fritzing sketch 07_pir_hareket (saved by Fritzing 0.9.5d)
breadboards: 1

parts:
  Parça1 = Arduino Uno (Rev3)
  PIR1 = PIR sensor

nets:
  N1: Parça1.D8, PIR1.SIG
  5V: Parça1.5V, PIR1.VDD
  GND: Parça1.GND, PIR1.GND
