# Fritzing sketch 08_ldr_isik (saved by Fritzing 0.9.5d)
breadboards: 1

parts:
  Parça1 = Arduino Uno (Rev3)
  R1 = Resistor [tolerance=±5% resistance=330 package=THT]
  R2 = Resistor [tolerance=±5% resistance=10k package=THT]
  R3 = Photocell (LDR) [package=THT]
  LED1 = LED - 5mm [color="Red (633nm)" package="5 mm [THT]"]

nets:
  N1: Parça1.A0, R2.Pin_1, R3.pin_0
  N2: Parça1.GND, R2.Pin_0, LED1.cathode
  N3: Parça1.D3_PWM, R1.Pin_1
  N4: Parça1.5V, R3.pin_1
  N5: R1.Pin_0, LED1.anode
