# Fritzing sketch 09_buzzer (saved by Fritzing 0.9.5d)
breadboards: 1

parts:
  Parça1 = Arduino Uno (Rev3)
  R1 = Resistor [tolerance=±5% resistance=220 package=THT]
  J1 = Piezo Speaker

nets:
  N1: Parça1.D2, J1.pin2
  N2: Parça1.GND, R1.Pin_0
  N3: R1.Pin_1, J1.pin1
