# Fritzing sketch 10_toprak_nem (saved by Fritzing 0.9.5d)
breadboards: 1

parts:
  Parça1 = Arduino Uno (Rev3)
  J1 = Piezo Speaker
  Parça2 = FC-28 Soil Hygrometer Module - Probe
  Parça3 = FC-28 Soil Hygrometer Module
  R1 = Resistor [tolerance=±5% resistance=330 package=THT]

nets:
  N1: Parça1.D8, J1.pin2
  N2: Parça1.D9_PWM, Parça3.DO
  5V: Parça1.5V, Parça3.VCC
  GND: Parça1.GND, Parça3.GND, R1.Pin_1
  N3: J1.pin1, R1.Pin_0
  N4: Parça2.POS, Parça3.POS
  N5: Parça2.NEG, Parça3.NEG

custom parts:
  FC-28 Soil Hygrometer Module - Probe: The FC-28 is a soil hygrometer module that uses the Texas Instruments LM393 comparator chip to provide an analog measurement of soil humidity.
  FC-28 Soil Hygrometer Module: The FC-28 is a soil hygrometer module that uses the Texas Instruments LM393 comparator chip to provide an analog measurement of soil humidity. The digital output is high when soil moisture is over a certain threshold, as determined by adjusting the potentiometer.
