# Fritzing sketch 01_blink (saved by Fritzing 0.9.5d)
breadboards: 1

parts:
  R2 = Resistor [tolerance=±5% resistance=330 package=THT]
  LED1 = LED - 5mm [color="Red (633nm)" package="5 mm [THT]"]
  Parça1 = Arduino Uno (Rev3)

nets:
  N1: R2.Pin_0, LED1.anode
  N2: R2.Pin_1, Parça1.D13/SCK
  N3: LED1.cathode, Parça1.GND
